# Fritzing sketch sketch (saved by Fritzing 0.9.3b)
perfboards: 1

parts:
  5v_Regulator = Voltage Regulator [package=to-220-alt]
  Input_power = Power Jack [package=power_jack_smd]
  Snorkel_stepper = Stepper Motor - Bipolar
  Trick_or_treat_button = Round Pushbutton
  Sound_bytes_button = Round Pushbutton
  Snorkel_button = Round Pushbutton
  Light_switch = SWITCH_SPDT [package=kps-1290]
  Snorkel_limit_sw2 = SWITCH-MOMENTARY-2 [package=tactile-switch-1101ne]
  Snorkel_limit_sw1 = SWITCH-MOMENTARY-2 [package=tactile-switch-1101ne]
  To_lights = Basic FET N-Channel [package="TO220 [THT]"]
  To_flashers = Basic FET N-Channel [package="TO220 [THT]"]
  Pololu_A2 = DRV 8825 Stepper Motor Carrier, High Current [part_number="DRV 8825"]
  Controller = Arduino Uno (Rev3)
  Headlights_and_side_markers = LED - 5mm [color="White (6500K)" package="5 mm [THT]"]
  Flashers = LED - 5mm [color="White (6500K)" package="5 mm [THT]"]
  To_snorkel_blower = Basic FET N-Channel [package="TO220 [THT]"]
  Snorkel_Blower = DC Motor

nets:
  GND: 5v_Regulator.GND, Input_power.GND, Trick_or_treat_button.leg0, Sound_bytes_button.leg0, Snorkel_button.leg0, Light_switch.P, Snorkel_limit_sw2.1, Snorkel_limit_sw1.1, To_lights.source, To_flashers.source, Pololu_A2.GROUND_LOG, Controller.GND, To_snorkel_blower.source
  N1: 5v_Regulator.IN, Input_power.PWR, Pololu_A2.VOLTAGE_ST/_MT, Headlights_and_side_markers.anode, Flashers.anode
  N2: 5v_Regulator.OUT, Controller.5V, Snorkel_Blower.pin_1
  N3: Snorkel_stepper.A, Pololu_A2.OUT_2B
  N4: Snorkel_stepper.C, Pololu_A2.OUT_2A
  N5: Snorkel_stepper.B, Pololu_A2.OUT_1A
  N6: Snorkel_stepper.D, Pololu_A2.OUT_1B
  N7: Trick_or_treat_button.leg1, Controller.A1
  N8: Sound_bytes_button.leg1, Controller.A2
  N9: Snorkel_button.leg1, Controller.A3
  N10: Light_switch.S, Controller.A0
  N11: Snorkel_limit_sw2.2, Snorkel_limit_sw1.2, Controller.D9_PWM
  N12: To_lights.gate, Controller.D6_PWM
  N13: To_lights.drain, Headlights_and_side_markers.cathode
  N14: To_flashers.gate, Controller.D8
  N15: To_flashers.drain, Flashers.cathode
  N16: Pololu_A2.ENABLE, Controller.D7, To_snorkel_blower.gate
  N17: Pololu_A2.STEP, Controller.A4/SDA
  N18: Pololu_A2.DIRECTION, Controller.A5/SCL
  N19: To_snorkel_blower.drain, Snorkel_Blower.pin_2
